// Logisim project s-mips.circ as structural Verilog: 25 circuits, main circuit S-MIPS Board
module ALU_Selector (
  input  in_1,
  input  in_2,
  input  in_3,
  input  in_4,
  input  in_5,
  input  in_6,
  input  in_7,
  input  in_8,
  input  in_9,
  input  in_10,
  input  in_11,
  input  in_12,
  input  in_13,
  input  in_14,
  input  in_15,
  input  in_16,
  input  in_17,
  input  in_18,
  output Signo,
  output Inmediate,
  output [3:0] Selector
);

  wire priority_encoder_1_p5, priority_encoder_1_p6, priority_encoder_1_p7, priority_encoder_1_p8,
       priority_encoder_1_p9, priority_encoder_1_p11;

  or or_1 (Signo, in_5, in_3, in_7, in_14);
  or or_2 (Inmediate, in_14, in_13, in_17, in_16, in_18);
  // Priority_Encoder #(.select(4)) priority_encoder_1: pin names not known; wires that end beside it: Selector, 1'b1, 1'b1, in_2, priority_encoder_1_p5, priority_encoder_1_p6, priority_encoder_1_p7, priority_encoder_1_p8, priority_encoder_1_p9, in_11, priority_encoder_1_p11
  or or_3 (priority_encoder_1_p5, in_3, in_4);
  or or_4 (priority_encoder_1_p6, in_5, in_6);
  or or_5 (priority_encoder_1_p9, in_10, in_17);
  or or_6 (priority_encoder_1_p11, in_12, in_18);
  or or_7 (priority_encoder_1_p7, in_7, in_8, in_15, in_14);
  or or_8 (priority_encoder_1_p8, in_9, in_16);

  // Other names for the same wires on the sheet: add = in_1; addi = in_13; and = in_9; andi = in_16; div = in_5;
  //   divu = in_6; mult = in_3; mulu = in_4; nor = in_11; or = in_10; ori = in_17; slt = in_7; slti = in_14;
  //   sltiu = in_15; sltu = in_8; sub = in_2; xor = in_12; xori = in_18
endmodule

module S_MIPS_Board (
  input  DESHABILITAR_DISPATCHER,
  output halt
);

  wire button_1_out, CLK, CS, d_ff_1_q, LCLR, LoadRAM, LoadRAMOn, LW, R_R_W, R_W, ram_dispatcher_1_finished,
       RCS, Reset_out, RST, TTY_EN;
  wire [2:0] KDB;
  wire [3:0] LMask, Mask, ram_1_read_time, ram_1_write_time, RMask;
  wire [6:0] KDB_DATA, TTY_DATA;
  wire [15:0] Addr, LAddr, RAddr;
  wire [31:0] I0, I1, I2, I3, LData, ram_1_data_out_0, ram_1_data_out_1, ram_1_data_out_2, ram_1_data_out_3,
       RI0, RI1, RI2, RI3;

  TTY #(.rows(25), .cols(80)) tty_1 (.data(TTY_DATA), .clk(CLK), .we(TTY_EN), .clr(RST));
  not not_1 (LoadRAMOn, ram_dispatcher_1_finished);
  RAM_Dispatcher ram_dispatcher_1 (
    .WriteTime(ram_1_write_time), .Clock(CLK), .Data(LData), .Address(LAddr), .Mask(LMask),
    .Finished(ram_dispatcher_1_finished), .Write(LW), .CLR(LCLR));
  Keyboard #(.buflen(64)) keyboard_1 (.clk(CLK), .re(KDB[0]), .avail(KDB[2]), .data(KDB_DATA));  // open: clr
  RAM ram_1 (
    .Address(RAddr), .Data_Out_0(ram_1_data_out_0), .Data_Out_1(ram_1_data_out_1),
    .Data_Out_2(ram_1_data_out_2), .Data_Out_3(ram_1_data_out_3), .Data_In_0(RI0), .Data_In_1(RI1),
    .Data_In_2(RI2), .Data_In_3(RI3), .Mask(RMask), .nRead_Write(R_R_W), .Chip_Select(RCS),
    .Read_Time(ram_1_read_time), .Reset(button_1_out), .Write_Time(ram_1_write_time));
  Button button_1 (.out(button_1_out));
  D_Flip_Flop d_ff_1 (.clk(CLK), .D(1'b1), .Q(d_ff_1_q), .reset(Reset_out));  // open: Qn, preset, en
  Button Reset (.out(Reset_out));
  S_MIPS s_mips_1 (
    .Kbd_Enable(KDB[0]), .Address(Addr), .Kbd_Clear(KDB[1]), .Kbd_Available(KDB[2]), .RAM_In_0(I0),
    .Kbd_ASCII_Data(KDB_DATA), .RAM_In_1(I1), .TTY_Enable(TTY_EN), .RAM_In_2(I2), .RAM_In_3(I3),
    .TTY_ASCII_Data(TTY_DATA), .Reset(RST), .RAM_Out_0(ram_1_data_out_0), .Clock(CLK),
    .RAM_Out_1(ram_1_data_out_1), .Stop(halt), .RAM_Out_2(ram_1_data_out_2), .RAM_Out_3(ram_1_data_out_3),
    .Mask(Mask), .Read_Time(ram_1_read_time), .Write_Time(ram_1_write_time), .nRead_Write(R_W),
    .Chip_Select(CS));
  D_Flip_Flop d_ff_2 (.clk(CLK), .D(d_ff_1_q), .Qn(LCLR), .reset(Reset_out));  // open: Q, preset, en
  or or_1 (RST, LCLR, LoadRAM);
  Clock clock_1 (.out(CLK));
  Multiplexer #(.width(32), .enable("false")) multiplexer_1 (.in0(I0), .in1(LData), .out(RI0), .sel(LoadRAM));
  Multiplexer #(.width(32), .enable("false")) multiplexer_2 (.in0(I1), .in1(LData), .out(RI1), .sel(LoadRAM));
  Multiplexer #(.width(32), .enable("false")) multiplexer_3 (.in0(I2), .in1(LData), .out(RI2), .sel(LoadRAM));
  Multiplexer #(.width(32), .enable("false")) multiplexer_4 (.in0(I3), .in1(LData), .out(RI3), .sel(LoadRAM));
  and and_1 (LoadRAM, ~DESHABILITAR_DISPATCHER, LoadRAMOn);  // AND_Gate
  Multiplexer #(.width(16), .enable("false")) multiplexer_5 (.in0(Addr), .in1(LAddr), .out(RAddr), .sel(LoadRAM));
  Multiplexer #(.width(4), .enable("false")) multiplexer_6 (.in0(Mask), .in1(LMask), .out(RMask), .sel(LoadRAM));
  Multiplexer #(.enable("false")) multiplexer_7 (.in0(CS), .in1(LW), .out(RCS), .sel(LoadRAM));
  Multiplexer #(.enable("false")) multiplexer_8 (.in0(R_W), .in1(LW), .out(R_R_W), .sel(LoadRAM));

  // Notes on the sheet:
  //   NO MODIFICAR
  //   Keyboard
endmodule

module RAM (
  input  [15:0] Address,
  input  [31:0] Data_In_0,
  input  [31:0] Data_In_1,
  input  [31:0] Data_In_2,
  input  [31:0] Data_In_3,
  input  [3:0] Mask,
  input  nRead_Write,
  input  Chip_Select,
  input  Reset,
  output [31:0] Data_Out_0,
  output [31:0] Data_Out_1,
  output [31:0] Data_Out_2,
  output [31:0] Data_Out_3,
  output [3:0] Read_Time,
  output [3:0] Write_Time
);

  wire and_2_out, and_3_out, and_4_out, and_5_out, and_6_out, and_7_out, and_8_out, and_9_out, Changed, CLK,
       comparator_2_eq, comparator_3_eq, comparator_4_eq, comparator_5_eq, comparator_6_eq, Count,
       demultiplexer_3_out0, Idle, Idle_q, Load, Load0, Load1, nand_1_out, or_1_out, or_2_out, or_3_out,
       or_4_out, or_5_out, or_6_out, or_7_out, or_8_out, or_9_out, or_10_out, Proc_q, Update_Mem, Zero_Time;
  wire [3:0] counter_1_q, multiplexer_1_out, subtractor_1_out;
  wire [31:0] register_1_q, register_2_q, register_3_q, register_4_q, register_5_q;

  // Probe on 4'b0011
  // Probe on 4'b0010
  Multiplexer #(.width(4), .enable("false")) multiplexer_1 (
    .in0(4'b0011), .in1(4'b0010), .out(multiplexer_1_out), .sel(nRead_Write));
  or or_1 (or_1_out, Idle, Update_Mem);
  or or_2 (or_2_out, ~Chip_Select, Reset);  // OR_Gate
  Subtractor #(.width(4)) subtractor_1 (.a(multiplexer_1_out), .b(4'b0010), .out(subtractor_1_out));  // open: bin, bout
  Demultiplexer #(.enable("false")) demultiplexer_1 (.out0(Idle), .out1(Load0), .in(Idle_q), .sel(Changed));
  D_Flip_Flop u_Idle (.clk(CLK), .D(or_1_out), .Q(Idle_q), .preset(or_2_out));  // open: Qn, en, reset
  // Probe on counter_1_q
  Counter #(.width(4), .max('hf)) counter_1 (
    .load(Load), .D(subtractor_1_out), .count(Count), .Q(counter_1_q), .clk(CLK), .clr(or_3_out));  // open: carry
  or or_3 (or_3_out, ~Chip_Select, Reset);  // OR_Gate
  Comparator #(.width(4), .mode("unsigned")) comparator_1 (
    .a(4'b0000), .b(counter_1_q), .eq(Zero_Time));  // open: gt, lt
  or or_4 (or_4_out, Count, Load0, Load1);
  Register #(.width(32)) register_1 (.D(Data_In_0), .en(Chip_Select), .Q(register_1_q), .clk(CLK), .clr(or_5_out));
  or or_5 (or_5_out, ~Chip_Select, Reset);  // OR_Gate
  Register #(.width(32)) register_2 (.D(Data_In_1), .en(Chip_Select), .Q(register_2_q), .clk(CLK), .clr(or_6_out));
  or or_6 (or_6_out, ~Chip_Select, Reset);  // OR_Gate
  Register #(.width(32)) register_3 (.D(Data_In_2), .en(Chip_Select), .Q(register_3_q), .clk(CLK), .clr(or_7_out));
  or or_7 (or_7_out, ~Chip_Select, Reset);  // OR_Gate
  Register #(.width(32)) register_4 (.D(Data_In_3), .en(Chip_Select), .Q(register_4_q), .clk(CLK), .clr(or_8_out));
  or or_8 (or_8_out, ~Chip_Select, Reset);  // OR_Gate
  Register #(.width(32)) register_5 (
    .D({{11{1'b1}}, nRead_Write, Mask, Address}), .en(Chip_Select), .Q(register_5_q), .clk(CLK),
    .clr(or_9_out));
  or or_9 (or_9_out, ~Chip_Select, Reset);  // OR_Gate
  D_Flip_Flop Proc (.clk(CLK), .D(or_4_out), .Q(Proc_q), .reset(or_10_out));  // open: Qn, preset, en
  or or_10 (or_10_out, ~Chip_Select, Reset);  // OR_Gate
  Demultiplexer #(.enable("false")) demultiplexer_2 (
    .out0(Count), .out1(Update_Mem), .in(demultiplexer_3_out0), .sel(Zero_Time));
  Demultiplexer #(.enable("false")) demultiplexer_3 (
    .out0(demultiplexer_3_out0), .out1(Load1), .in(Proc_q), .sel(Changed));
  Clock clock_1 (.out(CLK));
  Comparator #(.width(32)) comparator_2 (.a(register_1_q), .b(Data_In_0), .eq(comparator_2_eq));  // open: gt, lt
  Comparator #(.width(32)) comparator_3 (.a(register_2_q), .b(Data_In_1), .eq(comparator_3_eq));  // open: gt, lt
  Comparator #(.width(32)) comparator_4 (.a(register_3_q), .b(Data_In_2), .eq(comparator_4_eq));  // open: gt, lt
  Comparator #(.width(32)) comparator_5 (.a(register_4_q), .b(Data_In_3), .eq(comparator_5_eq));  // open: gt, lt
  Comparator #(.width(32)) comparator_6 (
    .a(register_5_q), .b({{11{1'b1}}, nRead_Write, Mask, Address}), .eq(comparator_6_eq));  // open: gt, lt
  nand nand_1 (nand_1_out, comparator_6_eq, comparator_2_eq, comparator_3_eq, comparator_4_eq, comparator_5_eq);
  and and_1 (Changed, nand_1_out, Chip_Select);
  or or_11 (Load, Count, Load1, Load0);
  and and_2 (and_2_out, Mask[0], Update_Mem, nRead_Write);
  and and_3 (and_3_out, Mask[1], Update_Mem, nRead_Write);
  and and_4 (and_4_out, Mask[2], Update_Mem, nRead_Write);
  and and_5 (and_5_out, Mask[3], Update_Mem, nRead_Write);
  RAM_part #(.addrWidth(16), .dataWidth(32), .bus("separate")) ram_1 (
    .addr(Address), .din(Data_In_0), .data(Data_Out_0), .str(and_2_out), .sel(Chip_Select), .clk(CLK),
    .ld(and_6_out), .clr(Reset));
  and and_6 (and_6_out, ~nRead_Write, Idle);  // AND_Gate
  RAM_part #(.addrWidth(16), .dataWidth(32), .bus("separate")) ram_2 (
    .addr(Address), .din(Data_In_1), .data(Data_Out_1), .str(and_3_out), .sel(Chip_Select), .clk(CLK),
    .ld(and_7_out), .clr(Reset));
  and and_7 (and_7_out, ~nRead_Write, Idle);  // AND_Gate
  RAM_part #(.addrWidth(16), .dataWidth(32), .bus("separate")) ram_3 (
    .addr(Address), .din(Data_In_2), .data(Data_Out_2), .str(and_4_out), .sel(Chip_Select), .clk(CLK),
    .ld(and_8_out), .clr(Reset));
  and and_8 (and_8_out, ~nRead_Write, Idle);  // AND_Gate
  RAM_part #(.addrWidth(16), .dataWidth(32), .bus("separate")) ram_4 (
    .addr(Address), .din(Data_In_3), .data(Data_Out_3), .str(and_5_out), .sel(Chip_Select), .clk(CLK),
    .ld(and_9_out), .clr(Reset));
  and and_9 (and_9_out, ~nRead_Write, Idle);  // AND_Gate

  assign Read_Time = 4'b0011;
  assign Write_Time = 4'b0010;

  // Other names for the same wires on the sheet: M0 = Mask[0]; M1 = Mask[1]; M2 = Mask[2]; M3 = Mask[3];
  //   RW = nRead_Write; CLR = Reset; CS = Chip_Select; Load2 = Count

  // Notes on the sheet:
  //   NO MODIFICAR
  //   excepto quizás los valores RT y WT
  //   BANK0
  //   BANK1
  //   BANK2
  //   BANK3
endmodule

module S_MIPS (
  input  Kbd_Available,
  input  [6:0] Kbd_ASCII_Data,
  input  [31:0] RAM_Out_0,
  input  [31:0] RAM_Out_1,
  input  Reset,
  input  [31:0] RAM_Out_2,
  input  Clock,
  input  [31:0] RAM_Out_3,
  input  [3:0] Read_Time,
  input  [3:0] Write_Time,
  output Kbd_Enable,
  output [15:0] Address,
  output Kbd_Clear,
  output TTY_Enable,
  output [6:0] TTY_ASCII_Data,
  output Stop,
  output [31:0] RAM_In_0,
  output [31:0] RAM_In_1,
  output [31:0] RAM_In_2,
  output [31:0] RAM_In_3,
  output [3:0] Mask,
  output nRead_Write,
  output Chip_Select
);

  wire ALU_Inst, d_ff_2_q, get_DATA, get_Inst, halt, jump_Inst, mem_Inst, or_1_out, or_2_out, R_Inst,
       Ready_Data, Ready_Inst, stack_Inst, START, tty_Inst, use_GI, use_PC, use_RF, write, Write_Inst,
       Write_Ready;
  wire [31:0] ADD, data_path_1_r_output, Ins_DATA, multiplexer_1_out, multiplexer_2_out, multiplexer_3_out,
       multiplexer_4_out, using_ram_1_out_14, using_ram_1_out_16, using_ram_1_out_18, using_ram_1_out_22;

  D_Flip_Flop #(.trigger("falling")) d_ff_1 (.clk(Clock), .D(Reset), .Q(START));  // open: Qn, preset, en, reset
  or or_1 (or_1_out, mem_Inst, stack_Inst);
  Multiplexer #(.width(32)) multiplexer_1 (
    .in0(RAM_Out_0), .in1(RAM_In_0), .out(multiplexer_1_out), .sel(write));  // open: en
  Multiplexer #(.width(32)) multiplexer_2 (
    .in0(RAM_Out_1), .in1(RAM_In_0), .out(multiplexer_2_out), .sel(write));  // open: en
  Multiplexer #(.width(32)) multiplexer_3 (
    .in0(RAM_Out_2), .in1(RAM_In_0), .out(multiplexer_3_out), .sel(write));  // open: en
  Multiplexer #(.width(32)) multiplexer_4 (
    .in0(RAM_Out_3), .in1(RAM_In_0), .out(multiplexer_4_out), .sel(write));  // open: en
  Control_Unit control_unit_1 (
    .Tic(Clock), .tty_Inst(tty_Inst), .start(START), .Ready_Data(Ready_Data), .Ready_Inst(Ready_Inst),
    .ALU_Inst(ALU_Inst), .jump_Inst(jump_Inst), .memor_Inst(or_1_out), .R_Inst(R_Inst),
    .Write_Inst(Write_Inst), .reset(Reset), .Write_Ready(Write_Ready), .out_13(Kbd_Enable), .out_14(write),
    .out_15(use_PC), .out_16(use_RF), .en_tty(TTY_Enable), .out_18(get_Inst), .out_19(use_GI),
    .out_20(get_DATA), .out_21(Stop));
  Using_RAM using_ram_1 (
    .RAM_0(multiplexer_1_out), .Tic(Clock), .Reset(Reset), .Write(write), .RAM_1(multiplexer_2_out),
    .get_Ins(get_Inst), .get_DATA(get_DATA), .is_Ins(use_GI), .RAM_2(multiplexer_3_out),
    .RAM_3(multiplexer_4_out), .DP_Address(ADD), .Write_Time(Write_Time), .Read_Time(Read_Time),
    .out_14(using_ram_1_out_14), .R_W(nRead_Write), .out_16(using_ram_1_out_16), .Chip_Selecty(Chip_Select),
    .out_18(using_ram_1_out_18), .Rd_Inst(Ready_Inst), .Rd_Data(Ready_Data), .Rd_Write(Write_Ready),
    .out_22(using_ram_1_out_22), .ADDR(Address), .MASK(Mask));
  or or_2 (or_2_out, get_Inst, Ready_Inst);
  D_Flip_Flop #(.trigger("falling")) d_ff_2 (
    .clk(Clock), .D(get_Inst), .Q(d_ff_2_q), .en(or_2_out));  // open: Qn, preset, reset
  Multiplexer #(.select(2), .width(32)) multiplexer_5 (
    .in0(using_ram_1_out_14), .in1(using_ram_1_out_16), .in2(using_ram_1_out_18), .in3(using_ram_1_out_22),
    .out(Ins_DATA), .sel(ADD[3:2]));  // open: en
  Data_Path data_path_1 (
    .kbd_ok(Kbd_Available), .in_2(Ins_DATA), .enablePC(use_PC), .Next_instrc(d_ff_2_q),
    .in_5(Kbd_ASCII_Data), .enableGI(use_GI), .in_7(Clock), .RF(use_RF), .Reset(Reset), .ADDRESS(ADD),
    .Jump_Inst(jump_Inst), .R_Output(data_path_1_r_output), .R_Inst(R_Inst), .Stack_Inst(stack_Inst),
    .tty_Data(TTY_ASCII_Data), .ALU_Inst(ALU_Inst), .Write_Inst(Write_Inst), .Memory_Inst(mem_Inst),
    .tty(tty_Inst), .halt(halt));
  Inv inv_1 (.Input(data_path_1_r_output), .Output(RAM_In_0));

  assign Kbd_Clear = Clock;
  assign RAM_In_1 = RAM_In_0;
  assign RAM_In_2 = RAM_In_0;
  assign RAM_In_3 = RAM_In_0;

  // Other names for the same wires on the sheet: CLR = Reset; CS = Chip_Select; KBD_AVAIL = Kbd_Available;
  //   CLK = Clock; KBD_CLR = Clock; KBD_DATA[6:0] = Kbd_ASCII_Data; RAM_A[15:0] = Address; RAM_MASK[3:0] = Mask;
  //   RAM_INPUT_0[31:0] = RAM_In_0; RAM_INPUT_1[31:0] = RAM_In_0; RAM_INPUT_2[31:0] = RAM_In_0;
  //   RAM_INPUT_3[31:0] = RAM_In_0; RAM_Out[31:0] = RAM_In_0; RAM_OUTPUT_0[31:0] = RAM_Out_0;
  //   RAM_OUTPUT_1[31:0] = RAM_Out_1; RAM_OUTPUT_2[31:0] = RAM_Out_2; RAM_OUTPUT_3[31:0] = RAM_Out_3;
  //   RW = nRead_Write; TTY_DATA[6:0] = TTY_ASCII_Data

  // Notes on the sheet:
  //   RAM ADDRESS
  //   DATA FROM RAM
  //   DATA TO RAM
  //   DATA WRITE MASK
  //   RAM TIMING
  //   RAM CONTROL
  //   KEYBOARD
  //   TTY
  //   SEQUENCING
endmodule

module RAM_Dispatcher (
  input  [3:0] WriteTime,
  input  Clock,
  input  CLR,
  output [31:0] Data,
  output [15:0] Address,
  output [3:0] Mask,
  output Finished,
  output Write
);

  wire demultiplexer_2_out1, demultiplexer_3_out1, End, IDLE_q, IncAddr, Load, or_1_out, or_2_out, While_q,
       WriteEnd;
  wire [3:0] counter_1_q;
  wire [31:0] CurrentAddress_q;

  Counter #(.width(32), .max('hffffffff)) CurrentAddress (
    .count(IncAddr), .Q({CurrentAddress_q[31:18], Address, CurrentAddress_q[1:0]}), .clk(Clock), .clr(CLR));  // open: load, D, carry
  or or_1 (or_1_out, IncAddr, demultiplexer_3_out1, Finished);
  D_Flip_Flop IDLE (.clk(Clock), .D(or_1_out), .Q(IDLE_q), .preset(CLR));  // open: Qn, en, reset
  Demultiplexer #(.enable("false")) demultiplexer_1 (.out0(Load), .out1(Finished), .in(IDLE_q), .sel(End));
  D_Flip_Flop While (.clk(Clock), .D(or_2_out), .Q(While_q), .reset(CLR));  // open: Qn, preset, en
  or or_2 (or_2_out, Write, Load);
  RAM_part #(.addrWidth(18), .dataWidth(32)) ram_1 (
    .addr({Address, CurrentAddress_q[1:0]}), .data(Data), .clk(Clock));  // open: sel, ld, clr
  Demultiplexer #(.enable("false")) demultiplexer_2 (
    .out0(Write), .out1(demultiplexer_2_out1), .in(While_q), .sel(WriteEnd));
  Decoder #(.select(2)) decoder_1 (
    .out0(Mask[0]), .out1(Mask[1]), .out2(Mask[2]), .out3(Mask[3]), .sel(CurrentAddress_q[1:0]));  // open: en
  Demultiplexer #(.enable("false")) demultiplexer_3 (
    .out0(IncAddr), .out1(demultiplexer_3_out1), .in(demultiplexer_2_out1), .sel(End));
  Counter #(.width(4), .max('hf)) counter_1 (
    .load(Load), .D(WriteTime), .count(Write), .Q(counter_1_q), .clk(Clock));  // open: carry, clr
  Comparator #(.width(32)) comparator_1 (.a(Data), .b({32{1'b1}}), .eq(End));  // open: gt, lt
  Comparator #(.width(4)) comparator_2 (.a(4'b0000), .b(counter_1_q), .eq(WriteEnd));  // open: gt, lt

  // Other names for the same wires on the sheet: CLK = Clock; Count = Write; WT[3:0] = WriteTime
endmodule

module Complemento_a_2 (
  input  [31:0] in_1,
  output [31:0] Output
);

  wire [31:0] not_1_out;

  assign not_1_out = ~in_1;  // NOT_Gate not_1, 32 bits wide
  Adder #(.width(32)) adder_1 (.a(not_1_out), .b(32'h1), .out(Output));  // open: cin, cout
endmodule

module ALU (
  input  [31:0] Input1,
  input  [31:0] Input2,
  input  in_3,
  input  in_4,
  input  [3:0] in_5,
  output [31:0] Output,
  output [31:0] Lower,
  output [31:0] High
);

  wire and_2_out, and_3_out, comparator_1_lt, comparator_2_lt, comparator_4_eq, Enable, ismult, or_2_out;
  wire [31:0] ADD, AND, Div, DivRest, Mulhig, Mulow, Mult_Div, multiplexer_2_out, NOR, OR, SUB, tunnel, XOR;

  Multiplexer #(.select(4), .width(32), .enable("false")) multiplexer_1 (
    .in0(ADD), .in1(SUB), .in2(Mult_Div), .in3(Mult_Div), .in4(tunnel), .in5(AND), .in6(OR), .in7(NOR),
    .in8(XOR), .out(Output), .sel(in_5));  // open: in9, in10, in11, in12, in13, in14, in15
  Adder #(.width(32)) adder_1 (.a(Input1), .b(Input2), .out(ADD));  // open: cin, cout
  Subtractor #(.width(32)) subtractor_1 (.a(Input1), .b(Input2), .out(SUB));  // open: bin, bout
  assign AND = Input1 & Input2;  // AND_Gate and_1, 32 bits wide
  assign OR = Input1 | Input2;  // OR_Gate or_1, 32 bits wide
  assign NOR = ~(Input1 | Input2);  // NOR_Gate nor_1, 32 bits wide
  assign XOR = Input1 ^ Input2;  // XOR_Gate xor_1, 32 bits wide
  Comparator #(.width(32)) comparator_1 (.a(Input1), .b(Input2), .lt(comparator_1_lt));  // open: gt, eq
  Comparator #(.width(32), .mode("unsigned")) comparator_2 (
    .a(Input1), .b(Input2), .lt(comparator_2_lt));  // open: gt, eq
  Multiplication multiplication_1 (.in_1(in_3), .Input1(Input1), .Input2(Input2), .out_4(Mulhig), .out_5(Mulow));
  Division division_1 (.Input1(Input1), .Input2(Input2), .in_3(in_3), .Lower(Div), .High(DivRest));
  Multiplexer #(.width(32)) multiplexer_2 (
    .in0(DivRest), .in1(Mulhig), .out(multiplexer_2_out), .sel(ismult));  // open: en
  and and_2 (and_2_out, comparator_1_lt, in_3);
  and and_3 (and_3_out, ~in_3, comparator_2_lt);  // AND_Gate
  Register #(.width(32)) u_HIGH (.D(multiplexer_2_out), .en(Enable), .Q(High), .clk(in_4));  // open: clr
  or or_2 (or_2_out, and_2_out, and_3_out);
  assign tunnel = {{31{1'b0}}, or_2_out};  // Bit_Extender bit_extender_1
  Comparator #(.width(4)) comparator_3 (.a(in_5), .b(4'b0010), .eq(ismult));  // open: gt, lt
  Comparator #(.width(4)) comparator_4 (.a(in_5), .b(4'b0011), .eq(comparator_4_eq));  // open: gt, lt
  or or_3 (Enable, ismult, comparator_4_eq);
  Register #(.width(32)) LOW (.D(Mult_Div), .en(Enable), .Q(Lower), .clk(in_4));  // open: clr
  Multiplexer #(.width(32)) multiplexer_3 (.in0(Div), .in1(Mulow), .out(Mult_Div), .sel(ismult));  // open: en

  // Other names for the same wires on the sheet: ALU_Select[3:0] = in_5; OH[31:0] = High; OL[31:0] = Lower;
  //   Out[31:0] = Output; Signo = in_3; Tic = in_4

  // Notes on the sheet:
  //   Entradas
  //   OPERACIONES
  //   REGISTROS HI Y LO
  //   ENABLE
endmodule

module Multiplication (
  input  in_1,
  input  [31:0] Input1,
  input  [31:0] Input2,
  output [31:0] out_4,
  output [31:0] out_5
);

  wire and_1_out, OF, OF1, Sig1, Sig2, sr_3_bit_31_old, sr_4_bit_31_old;
  wire [31:0] adder_1_out, adder_2_out, Hig1, Hig2, Hig2_F, Low1, Low2, Low2_F, R1, R2, R11, R22,
       sl_1_output, sl_2_output, sr_1_out_3, sr_2_out_3, sr_7_out_3, subtractor_1_out, Temp1, Temp2;

  and and_1 (and_1_out, Sig1, Sig2);
  Multiplier #(.width(32)) multiplier_1 (.a(Input1), .b(Input2), .out(Low1), .cout(Hig1));  // open: cin
  SL sl_1 (.Input(Input1), .Bit_31_new(1'b0), .Bit_0_old(Sig1), .Output(sl_1_output));
  SL sl_2 (.Input(Input2), .Bit_31_new(1'b0), .Bit_0_old(Sig2), .Output(sl_2_output));
  SR sr_1 (.Bit_0_new(and_1_out), .Input({32{1'b0}}), .out_3(sr_1_out_3));  // open: Bit_31_old
  Multiplexer #(.width(32)) multiplexer_1 (.in0({32{1'b0}}), .in1(Input2), .out(Temp2), .sel(Sig1));  // open: en
  Multiplexer #(.width(32)) multiplexer_2 (.in0(Low2_F), .in1(Low1), .out(out_5), .sel(in_1));  // open: en
  Multiplexer #(.width(32)) multiplexer_3 (.in0(Hig2_F), .in1(Hig1), .out(out_4), .sel(in_1));  // open: en
  Subtractor #(.width(32)) subtractor_1 (.a(Input1), .b(sr_1_out_3), .out(subtractor_1_out));  // open: bin, bout
  Multiplier #(.width(32)) multiplier_2 (.a(sl_1_output), .b(sl_2_output), .out(Low2), .cout(Hig2));  // open: cin
  Multiplexer #(.width(32)) multiplexer_4 (
    .in0({32{1'b0}}), .in1(subtractor_1_out), .out(Temp1), .sel(Sig2));  // open: en
  SR sr_2 (.Bit_0_new(OF), .Input({32{1'b0}}), .out_3(sr_2_out_3));  // open: Bit_31_old
  SR sr_3 (.Bit_0_new(1'b0), .Input(Low2), .out_3(R1), .Bit_31_old(sr_3_bit_31_old));
  SR sr_4 (.Bit_0_new(1'b0), .Input(R1), .out_3(R11), .Bit_31_old(sr_4_bit_31_old));
  Adder #(.width(32)) adder_1 (.a(R11), .b(Temp1), .out(adder_1_out), .cout(OF));  // open: cin
  Adder #(.width(32)) adder_2 (.a(R22), .b(sr_2_out_3), .out(adder_2_out));  // open: cin, cout
  SR sr_5 (.Bit_0_new(sr_3_bit_31_old), .Input(Hig2), .out_3(R2));  // open: Bit_31_old
  SR sr_6 (.Bit_0_new(sr_4_bit_31_old), .Input(R2), .out_3(R22));  // open: Bit_31_old
  Adder #(.width(32)) adder_3 (.a(Temp2), .b(adder_1_out), .out(Low2_F), .cout(OF1));  // open: cin
  Adder #(.width(32)) adder_4 (.a(adder_2_out), .b(sr_7_out_3), .out(Hig2_F));  // open: cin, cout
  SR sr_7 (.Bit_0_new(OF1), .Input({32{1'b0}}), .out_3(sr_7_out_3));  // open: Bit_31_old

  // Other names for the same wires on the sheet: High[31:0] = out_4; Lower[31:0] = out_5; Signo = in_1
endmodule

module Division (
  input  [31:0] Input1,
  input  [31:0] Input2,
  input  in_3,
  output [31:0] Lower,
  output [31:0] High
);

  wire Sig1, Sig2, xor_1_out;
  wire [31:0] complemento_a_2_1_output, divider_1_out, divider_1_rem, InpSig1, InpSig2, negator_1_out,
       negator_2_out, negator_3_out;

  Negator #(.width(32)) negator_1 (.in(Input1), .out(negator_1_out));
  Negator #(.width(32)) negator_2 (.in(Input2), .out(negator_2_out));
  Divider #(.width(32)) divider_1 (.a(InpSig1), .b(InpSig2), .out(divider_1_out), .rem(divider_1_rem));  // open: upper
  Complemento_a_2 complemento_a_2_1 (.in_1(divider_1_rem), .Output(complemento_a_2_1_output));
  Multiplexer #(.width(32)) multiplexer_1 (.in0(Input1), .in1(negator_1_out), .out(InpSig1), .sel(Sig1));  // open: en
  Multiplexer #(.width(32)) multiplexer_2 (.in0(Input2), .in1(negator_2_out), .out(InpSig2), .sel(Sig2));  // open: en
  Multiplexer #(.width(32)) multiplexer_3 (
    .in0(divider_1_out), .in1(negator_3_out), .out(Lower), .sel(xor_1_out));  // open: en
  Negator #(.width(32)) negator_3 (.in(divider_1_out), .out(negator_3_out));
  xor xor_1 (xor_1_out, Sig1, Sig2);
  Multiplexer #(.width(32)) multiplexer_4 (
    .in0(divider_1_rem), .in1(complemento_a_2_1_output), .out(High), .sel(Sig1));  // open: en
  and and_1 (Sig1, Input1[31], in_3);
  and and_2 (Sig2, in_3, Input2[31]);

  // Other names for the same wires on the sheet: Signo = in_3
endmodule

module Instruction_Decoder (
  input  [31:0] Instruccion,
  output nop,
  output add,
  output andi,
  output beq,
  output sw,
  output mfhi,
  output pop,
  output [4:0] out_9,
  output [4:0] out_10,
  output \and ,
  output sub,
  output ori,
  output bne,
  output jump,
  output mflo,
  output push,
  output [4:0] out_18,
  output \or ,
  output mult,
  output xori,
  output blez,
  output jr,
  output tty,
  output \nor ,
  output mulu,
  output addi,
  output bgtz,
  output slt,
  output rnd,
  output [25:0] out_31,
  output \xor ,
  output div,
  output slti,
  output bltz,
  output sltu,
  output kbd,
  output [15:0] out_38,
  output divu,
  output sltiu,
  output lw,
  output halt
);

  wire comparator_18_eq, comparator_19_eq, comparator_20_eq, comparator_21_eq, comparator_22_eq,
       comparator_23_eq, comparator_24_eq, comparator_25_eq, comparator_26_eq, comparator_27_eq,
       comparator_28_eq, comparator_29_eq, comparator_30_eq, comparator_31_eq, comparator_32_eq,
       comparator_33_eq, comparator_34_eq, comparator_35_eq, comparator_36_eq, comparator_37_eq,
       comparator_38_eq, comparator_39_eq, OP_0, OP_1, pop_push;

  Comparator #(.width(6)) comparator_1 (.a({6{1'b0}}), .b(Instruccion[31:26]), .eq(OP_0));  // open: gt, lt
  Comparator #(.width(6)) comparator_2 (.a({6{1'b1}}), .b(Instruccion[31:26]), .eq(OP_1));  // open: gt, lt
  Comparator #(.width(6)) comparator_3 (.a(6'b001000), .b(Instruccion[31:26]), .eq(addi));  // open: gt, lt
  Comparator #(.width(6)) comparator_4 (.a(6'b001010), .b(Instruccion[31:26]), .eq(slti));  // open: gt, lt
  Comparator #(.width(6)) comparator_5 (.a(6'b001011), .b(Instruccion[31:26]), .eq(sltiu));  // open: gt, lt
  Comparator #(.width(6)) comparator_6 (.a(6'b001100), .b(Instruccion[31:26]), .eq(andi));  // open: gt, lt
  Comparator #(.width(6)) comparator_7 (.a(6'b001101), .b(Instruccion[31:26]), .eq(ori));  // open: gt, lt
  Comparator #(.width(6)) comparator_8 (.a(6'b001110), .b(Instruccion[31:26]), .eq(xori));  // open: gt, lt
  Comparator #(.width(6)) comparator_9 (.a(6'b100011), .b(Instruccion[31:26]), .eq(lw));  // open: gt, lt
  Comparator #(.width(6)) comparator_10 (.a(6'b101011), .b(Instruccion[31:26]), .eq(sw));  // open: gt, lt
  Comparator #(.width(6)) comparator_11 (.a(6'b111000), .b(Instruccion[31:26]), .eq(pop_push));  // open: gt, lt
  Comparator #(.width(6)) comparator_12 (.a(6'b000100), .b(Instruccion[31:26]), .eq(beq));  // open: gt, lt
  Comparator #(.width(6)) comparator_13 (.a(6'b000101), .b(Instruccion[31:26]), .eq(bne));  // open: gt, lt
  Comparator #(.width(6)) comparator_14 (.a(6'b000110), .b(Instruccion[31:26]), .eq(blez));  // open: gt, lt
  Comparator #(.width(6)) comparator_15 (.a(6'b000111), .b(Instruccion[31:26]), .eq(bgtz));  // open: gt, lt
  Comparator #(.width(6)) comparator_16 (.a(6'b000001), .b(Instruccion[31:26]), .eq(bltz));  // open: gt, lt
  Comparator #(.width(6)) comparator_17 (.a(6'b000010), .b(Instruccion[31:26]), .eq(jump));  // open: gt, lt
  Comparator #(.width(6)) comparator_18 (.a({6{1'b0}}), .b(Instruccion[5:0]), .eq(comparator_18_eq));  // open: gt, lt
  Comparator #(.width(6)) comparator_19 (.a(6'b100000), .b(Instruccion[5:0]), .eq(comparator_19_eq));  // open: gt, lt
  Comparator #(.width(6)) comparator_20 (.a(6'b100010), .b(Instruccion[5:0]), .eq(comparator_20_eq));  // open: gt, lt
  Comparator #(.width(6)) comparator_21 (.a(6'b011000), .b(Instruccion[5:0]), .eq(comparator_21_eq));  // open: gt, lt
  Comparator #(.width(6)) comparator_22 (.a(6'b011001), .b(Instruccion[5:0]), .eq(comparator_22_eq));  // open: gt, lt
  Comparator #(.width(6)) comparator_23 (.a(6'b011010), .b(Instruccion[5:0]), .eq(comparator_23_eq));  // open: gt, lt
  Comparator #(.width(6)) comparator_24 (.a(6'b011011), .b(Instruccion[5:0]), .eq(comparator_24_eq));  // open: gt, lt
  Comparator #(.width(6)) comparator_25 (.a(6'b101010), .b(Instruccion[5:0]), .eq(comparator_25_eq));  // open: gt, lt
  Comparator #(.width(6)) comparator_26 (.a(6'b101011), .b(Instruccion[5:0]), .eq(comparator_26_eq));  // open: gt, lt
  and and_1 (nop, comparator_18_eq, OP_0);
  and and_2 (add, OP_0, comparator_19_eq);
  and and_3 (sub, comparator_20_eq, OP_0);
  and and_4 (mult, OP_0, comparator_21_eq);
  and and_5 (mulu, comparator_22_eq, OP_0);
  and and_6 (div, OP_0, comparator_23_eq);
  and and_7 (divu, comparator_24_eq, OP_0);
  and and_8 (slt, OP_0, comparator_25_eq);
  and and_9 (sltu, OP_0, comparator_26_eq);
  Comparator #(.width(6)) comparator_27 (.a(6'b100100), .b(Instruccion[5:0]), .eq(comparator_27_eq));  // open: gt, lt
  Comparator #(.width(6)) comparator_28 (.a(6'b100101), .b(Instruccion[5:0]), .eq(comparator_28_eq));  // open: gt, lt
  Comparator #(.width(6)) comparator_29 (.a(6'b100111), .b(Instruccion[5:0]), .eq(comparator_29_eq));  // open: gt, lt
  Comparator #(.width(6)) comparator_30 (.a(6'b101000), .b(Instruccion[5:0]), .eq(comparator_30_eq));  // open: gt, lt
  Comparator #(.width(6)) comparator_31 (.a(6'b001000), .b(Instruccion[5:0]), .eq(comparator_31_eq));  // open: gt, lt
  Comparator #(.width(6)) comparator_32 (.a(6'b010000), .b(Instruccion[5:0]), .eq(comparator_32_eq));  // open: gt, lt
  Comparator #(.width(6)) comparator_33 (.a(6'b010010), .b(Instruccion[5:0]), .eq(comparator_33_eq));  // open: gt, lt
  and and_10 (\and , comparator_27_eq, OP_0);
  and and_11 (\or , OP_0, comparator_28_eq);
  and and_12 (\nor , comparator_29_eq, OP_0);
  and and_13 (\xor , OP_0, comparator_30_eq);
  and and_14 (jr, comparator_31_eq, OP_0);
  and and_15 (mfhi, OP_0, comparator_32_eq);
  and and_16 (mflo, OP_0, comparator_33_eq);
  Comparator #(.width(6)) comparator_34 (.a({6{1'b1}}), .b(Instruccion[5:0]), .eq(comparator_34_eq));  // open: gt, lt
  Comparator #(.width(6)) comparator_35 (.a(6'b000001), .b(Instruccion[5:0]), .eq(comparator_35_eq));  // open: gt, lt
  Comparator #(.width(6)) comparator_36 (.a(6'b000010), .b(Instruccion[5:0]), .eq(comparator_36_eq));  // open: gt, lt
  Comparator #(.width(6)) comparator_37 (.a(6'b000100), .b(Instruccion[5:0]), .eq(comparator_37_eq));  // open: gt, lt
  Comparator #(.width(6)) comparator_38 (.a({6{1'b0}}), .b(Instruccion[5:0]), .eq(comparator_38_eq));  // open: gt, lt
  Comparator #(.width(6)) comparator_39 (.a(6'b000001), .b(Instruccion[5:0]), .eq(comparator_39_eq));  // open: gt, lt
  and and_17 (halt, comparator_34_eq, OP_1);
  and and_18 (tty, OP_1, comparator_35_eq);
  and and_19 (rnd, comparator_36_eq, OP_1);
  and and_20 (kbd, OP_1, comparator_37_eq);
  and and_21 (pop, comparator_38_eq, pop_push);
  and and_22 (push, pop_push, comparator_39_eq);

  assign out_9 = Instruccion[25:21];
  assign out_10 = Instruccion[20:16];
  assign out_18 = Instruccion[15:11];
  assign out_31 = Instruccion[25:0];
  assign out_38 = Instruccion[15:0];

  // Other names for the same wires on the sheet: Constante[15:0] = Instruccion[15:0];
  //   Destino[25:0] = Instruccion[25:0]; Func_Code[5:0] = Instruccion[5:0]; Rd[4:0] = Instruccion[15:11];
  //   Rt[4:0] = Instruccion[20:16]; Rs[4:0] = Instruccion[25:21]; OP_Code[5:0] = Instruccion[31:26]

  // Notes on the sheet:
  //   Entrada:
  //   OP-Code
  //   Salidas
  //   OP =  000000
  //   Func-Code
  //   OP =  111111
  //   OP=111000
endmodule

module SR (
  input  Bit_0_new,
  input  [31:0] Input,
  output [31:0] out_3,
  output Bit_31_old
);


  assign Bit_31_old = Input[31];
  assign out_3 = {Input[30:0], Bit_0_new};

  // Notes on the sheet:
  //   Shift Right
endmodule

module SL (
  input  [31:0] Input,
  input  Bit_31_new,
  output Bit_0_old,
  output [31:0] Output
);


  assign Bit_0_old = Input[0];
  assign Output = {Bit_31_new, Input[31:1]};

  // Notes on the sheet:
  //   Shift Left
endmodule

module Register_File (
  input  [31:0] in_1,
  input  in_2,
  input  in_3,
  input  in_4,
  input  in_5,
  input  in_6,
  input  in_7,
  input  [4:0] in_8,
  input  [4:0] in_9,
  input  [4:0] in_10,
  output [31:0] Output_A,
  output [31:0] Output_B,
  output [31:0] SP
);

  wire and_1_out, or_1_out, R0, R1, R2, R3, R4, R5, R6, R7, R8, R9, R10, R11, R12, R13, R14, R15, R16, R17,
       R18, R19, R20, R21, R22, R23, R24, R25, R26, R27, R28, R29, R30, R31, S31;
  wire [31:0] adder_1_out, multiplexer_1_out, multiplexer_2_out, O0, O1, O2, O3, O4, O5, O6, O7, O8, O9, O10,
       O11, O12, O13, O14, O15, O16, O17, O18, O19, O20, O21, O22, O23, O24, O25, O26, O27, O28, O29, O30,
       SP_t, subtractor_1_out;

  Register #(.width(32)) Reg0 (.D({32{1'b0}}), .en(1'b1), .Q(O0), .clk(in_3), .clr(in_2));
  Register #(.width(32)) Reg5 (.D(in_1), .en(R5), .Q(O5), .clk(in_3), .clr(in_2));
  Register #(.width(32)) Reg10 (.D(in_1), .en(R10), .Q(O10), .clk(in_3), .clr(in_2));
  Register #(.width(32)) Reg15 (.D(in_1), .en(R15), .Q(O15), .clk(in_3), .clr(in_2));
  Register #(.width(32)) Reg20 (.D(in_1), .en(R20), .Q(O20), .clk(in_3), .clr(in_2));
  Register #(.width(32)) Reg25 (.D(in_1), .en(R25), .Q(O25), .clk(in_3), .clr(in_2));
  Register #(.width(32)) Reg30 (.D(in_1), .en(R30), .Q(O30), .clk(in_3), .clr(in_2));
  Demultiplexer #(.select(5), .enable("false")) demultiplexer_1 (
    .out0(R0), .out1(R1), .out2(R2), .out3(R3), .out4(R4), .out5(R5), .out6(R6), .out7(R7), .out8(R8),
    .out9(R9), .out10(R10), .out11(R11), .out12(R12), .out13(R13), .out14(R14), .out15(R15), .out16(R16),
    .out17(R17), .out18(R18), .out19(R19), .out20(R20), .out21(R21), .out22(R22), .out23(R23), .out24(R24),
    .out25(R25), .out26(R26), .out27(R27), .out28(R28), .out29(R29), .out30(R30), .out31(S31), .in(in_4),
    .sel(in_8));
  Register #(.width(32)) Reg1 (.D(in_1), .en(R1), .Q(O1), .clk(in_3), .clr(in_2));
  Register #(.width(32)) Reg6 (.D(in_1), .en(R6), .Q(O6), .clk(in_3), .clr(in_2));
  Register #(.width(32)) Reg11 (.D(in_1), .en(R11), .Q(O11), .clk(in_3), .clr(in_2));
  Register #(.width(32)) Reg16 (.D(in_1), .en(R16), .Q(O16), .clk(in_3), .clr(in_2));
  Register #(.width(32)) Reg21 (.D(in_1), .en(R21), .Q(O21), .clk(in_3), .clr(in_2));
  Register #(.width(32)) Reg26 (.D(in_1), .en(R26), .Q(O26), .clk(in_3), .clr(in_2));
  Register #(.width(32)) Reg2 (.D(in_1), .en(R2), .Q(O2), .clk(in_3), .clr(in_2));
  Register #(.width(32)) Reg7 (.D(in_1), .en(R7), .Q(O7), .clk(in_3), .clr(in_2));
  Register #(.width(32)) Reg12 (.D(in_1), .en(R12), .Q(O12), .clk(in_3), .clr(in_2));
  Register #(.width(32)) Reg17 (.D(in_1), .en(R17), .Q(O17), .clk(in_3), .clr(in_2));
  Register #(.width(32)) Reg22 (.D(in_1), .en(R22), .Q(O22), .clk(in_3), .clr(in_2));
  Register #(.width(32)) Reg27 (.D(in_1), .en(R27), .Q(O27), .clk(in_3), .clr(in_2));
  Multiplexer #(.width(32), .enable("false")) multiplexer_1 (
    .in0(SP_t), .in1(in_1), .out(multiplexer_1_out), .sel(S31));
  Register #(.width(32)) u_SP (.D(multiplexer_1_out), .en(R31), .Q(SP), .clk(in_3));  // open: clr
  or or_1 (or_1_out, in_6, in_7);
  Subtractor #(.width(32)) subtractor_1 (.a(SP), .b(32'h4), .out(subtractor_1_out));  // open: bin, bout
  Adder #(.width(32)) adder_1 (.a(32'h4), .b(SP), .out(adder_1_out));  // open: cin, cout
  and and_1 (and_1_out, in_5, or_1_out);
  Multiplexer #(.width(32), .enable("false")) multiplexer_2 (
    .in0(subtractor_1_out), .in1(adder_1_out), .out(multiplexer_2_out), .sel(in_7));
  Register #(.width(32)) Reg3 (.D(in_1), .en(R3), .Q(O3), .clk(in_3), .clr(in_2));
  Register #(.width(32)) Reg8 (.D(in_1), .en(R8), .Q(O8), .clk(in_3), .clr(in_2));
  Register #(.width(32)) Reg13 (.D(in_1), .en(R13), .Q(O13), .clk(in_3), .clr(in_2));
  Register #(.width(32)) Reg18 (.D(in_1), .en(R18), .Q(O18), .clk(in_3), .clr(in_2));
  Register #(.width(32)) Reg23 (.D(in_1), .en(R23), .Q(O23), .clk(in_3), .clr(in_2));
  Register #(.width(32)) Reg28 (.D(in_1), .en(R28), .Q(O28), .clk(in_3), .clr(in_2));
  or or_2 (R31, in_2, S31, and_1_out);
  Multiplexer #(.width(32), .enable("false")) multiplexer_3 (
    .in0(multiplexer_2_out), .in1({32{1'b1}}), .out(SP_t), .sel(in_2));
  Register #(.width(32)) Reg4 (.D(in_1), .en(R4), .Q(O4), .clk(in_3), .clr(in_2));
  Register #(.width(32)) Reg9 (.D(in_1), .en(R9), .Q(O9), .clk(in_3), .clr(in_2));
  Register #(.width(32)) Reg14 (.D(in_1), .en(R14), .Q(O14), .clk(in_3), .clr(in_2));
  Register #(.width(32)) Reg19 (.D(in_1), .en(R19), .Q(O19), .clk(in_3), .clr(in_2));
  Register #(.width(32)) Reg24 (.D(in_1), .en(R24), .Q(O24), .clk(in_3), .clr(in_2));
  Register #(.width(32)) Reg29 (.D(in_1), .en(R29), .Q(O29), .clk(in_3), .clr(in_2));
  Multiplexer #(.select(5), .width(32), .enable("false")) multiplexer_4 (
    .in0(O0), .in1(O1), .in2(O2), .in3(O3), .in4(O4), .in5(O5), .in6(O6), .in7(O7), .in8(O8), .in9(O9),
    .in10(O10), .in11(O11), .in12(O12), .in13(O13), .in14(O14), .in15(O15), .in16(O16), .in17(O17),
    .in18(O18), .in19(O19), .in20(O20), .in21(O21), .in22(O22), .in23(O23), .in24(O24), .in25(O25),
    .in26(O26), .in27(O27), .in28(O28), .in29(O29), .in30(O30), .in31(SP), .out(Output_A), .sel(in_9));
  Multiplexer #(.select(5), .width(32), .enable("false")) multiplexer_5 (
    .in0(O0), .in1(O1), .in2(O2), .in3(O3), .in4(O4), .in5(O5), .in6(O6), .in7(O7), .in8(O8), .in9(O9),
    .in10(O10), .in11(O11), .in12(O12), .in13(O13), .in14(O14), .in15(O15), .in16(O16), .in17(O17),
    .in18(O18), .in19(O19), .in20(O20), .in21(O21), .in22(O22), .in23(O23), .in24(O24), .in25(O25),
    .in26(O26), .in27(O27), .in28(O28), .in29(O29), .in30(O30), .in31(SP), .out(Output_B), .sel(in_10));

  // Other names for the same wires on the sheet: inPC = in_5; Input[31:0] = in_1; O31[31:0] = SP; Pop = in_7;
  //   Push = in_6; Reset = in_2; SA[4:0] = in_9; SB[4:0] = in_10; Select[4:0] = in_8; Tic = in_3; Write_Read = in_4

  // Notes on the sheet:
  //   Inputs
  //   Seleccionar registro
  //   Trabajo con SP
  //   OUTPUTS
endmodule

module Inv (
  input  [31:0] Input,
  output [31:0] Output
);


  assign Output = {Input[7:0], Input[15:8], Input[23:16], Input[31:24]};
endmodule

module PC (
  input  [31:0] InPC,
  input  Enable,
  input  Tic,
  input  Reset,
  output [31:0] OutPC
);

  Register #(.width(32)) PC (.D(InPC), .en(Enable), .Q(OutPC), .clk(Tic), .clr(Reset));

  // Other names for the same wires on the sheet: En = Enable; Rst = Reset
endmodule

module Branch_Control (
  input  [25:0] in_1,
  input  beq,
  input  bne,
  input  [31:0] in_4,
  input  blez,
  input  bgtz,
  input  bltz,
  input  [31:0] in_8,
  input  jr,
  input  j,
  input  [31:0] in_11,
  input  [15:0] in_12,
  output [31:0] OUTPUT
);

  wire and_1_out, and_2_out, and_3_out, and_4_out, and_5_out, comparator_2_eq, priority_encoder_1_p4, RS_0,
       RS__0, RS_is_RT;
  wire [1:0] select;
  wire [13:0] bit_extender_1_out;
  wire [31:0] PC_4, PC_4_offset;

  Adder #(.width(32)) adder_1 (.a(in_11), .b(32'h4), .out(PC_4));  // open: cin, cout
  assign bit_extender_1_out = {{13{1'b0}}, in_12[15]};  // Bit_Extender bit_extender_1
  Adder #(.width(32)) adder_2 (.a(PC_4), .b({bit_extender_1_out, in_12, 2'b00}), .out(PC_4_offset));  // open: cin, cout
  // Priority_Encoder #(.select(2)) priority_encoder_1: pin names not known; wires that end beside it: select, 1'b1, 1'b1, priority_encoder_1_p4, j, jr
  or or_1 (priority_encoder_1_p4, and_1_out, and_2_out, and_3_out, and_4_out, and_5_out);
  Comparator #(.width(32)) comparator_1 (.a(in_4), .b(in_8), .eq(RS_is_RT));  // open: gt, lt
  Comparator #(.width(32)) comparator_2 (.a(in_4), .b({32{1'b0}}), .eq(comparator_2_eq), .lt(RS_0));  // open: gt
  and and_1 (and_1_out, beq, RS_is_RT);
  and and_2 (and_2_out, ~RS_is_RT, bne);  // AND_Gate
  and and_3 (and_3_out, blez, RS__0);
  and and_4 (and_4_out, ~RS__0, bgtz);  // AND_Gate
  and and_5 (and_5_out, bltz, RS_0);
  Multiplexer #(.select(2), .width(32), .enable("false")) multiplexer_1 (
    .in0(PC_4), .in1(PC_4_offset), .in2({in_11[31:28], in_1, 2'b00}), .in3(in_4), .out(OUTPUT), .sel(select));
  or or_2 (RS__0, comparator_2_eq, RS_0);

  // Other names for the same wires on the sheet: offset[15:0] = in_12; Destino[25:0] = in_1;
  //   Jump[31:2] = {in_11[31:28], in_1}; PC[31:0] = in_11; RS[31:0] = in_4; RT[31:0] = in_8

  // Notes on the sheet:
  //   INPUT
  //   Estándar
  //   Salto
endmodule

module RF_Selector (
  input  [31:0] in_1,
  input  [31:0] in_2,
  input  LW,
  input  pop,
  input  mfhi,
  input  [31:0] in_6,
  input  mflo,
  input  actKBD,
  input  [31:0] in_9,
  input  actRND,
  input  [31:0] in_11,
  input  [6:0] KBD,
  output [31:0] OUTPUT
);

  wire priority_encoder_1_p4;
  wire [2:0] Select;

  // Priority_Encoder priority_encoder_1: pin names not known; wires that end beside it: Select, 1'b1, 1'b1, priority_encoder_1_p4, mfhi, mflo, actRND, actKBD
  or or_1 (priority_encoder_1_p4, LW, pop);
  Multiplexer #(.select(3), .width(32), .enable("false")) multiplexer_1 (
    .in0(in_1), .in1(in_6), .in2(in_9), .in3(in_11), .in4(in_2), .in5({{25{1'b0}}, KBD}), .out(OUTPUT),
    .sel(Select));  // open: in6, in7

  // Other names for the same wires on the sheet: HI[31:0] = in_9; KBD_t[6:0] = KBD; LO[31:0] = in_11;
  //   Mem[31:0] = in_6; outALU[31:0] = in_1; RND[31:0] = in_2

  // Notes on the sheet:
  //   INPUTS
endmodule

module Memory_Addres (
  input  [31:0] in_1,
  input  pop,
  input  push,
  input  [31:0] in_4,
  input  LW,
  input  SW,
  input  isPC,
  input  [31:0] in_8,
  output [31:0] OUTPUT
);

  wire or_1_out, or_2_out;
  wire [1:0] priority_encoder_1_out;
  wire [31:0] multiplexer_1_out, subtractor_1_out;

  Subtractor #(.width(32)) subtractor_1 (.a(in_8), .b(32'h4), .out(subtractor_1_out));  // open: bin, bout
  Multiplexer #(.width(32), .enable("false")) multiplexer_1 (
    .in0(in_8), .in1(subtractor_1_out), .out(multiplexer_1_out), .sel(push));
  Multiplexer #(.select(2), .width(32), .enable("false")) multiplexer_2 (
    .in0(in_4), .in1(in_1), .in2(multiplexer_1_out), .in3(in_4), .out(OUTPUT), .sel(priority_encoder_1_out));
  Priority_Encoder #(.select(2)) priority_encoder_1 (
    .in0(1'b1), .in1(or_2_out), .in2(or_1_out), .in3(isPC), .out(priority_encoder_1_out));
  or or_1 (or_1_out, push, pop);
  or or_2 (or_2_out, SW, LW);

  // Other names for the same wires on the sheet: ALU[31:0] = in_1; PC[31:0] = in_4; SP[31:0] = in_8

  // Notes on the sheet:
  //   INPUT
endmodule

module Data_Path (
  input  kbd_ok,
  input  [31:0] in_2,
  input  enablePC,
  input  Next_instrc,
  input  [6:0] in_5,
  input  enableGI,
  input  in_7,
  input  RF,
  input  Reset,
  output [31:0] ADDRESS,
  output Jump_Inst,
  output [31:0] R_Output,
  output R_Inst,
  output Stack_Inst,
  output [6:0] tty_Data,
  output ALU_Inst,
  output Write_Inst,
  output Memory_Inst,
  output tty,
  output halt
);

  wire add, addi, \and , andi, beq, bgtz, blez, bltz, bne, div, divu, Inmediate, jr, jump, kbd, lw, mfhi,
       mflo, mult, mulu, nop, \nor , \or , or_1_out, ori, pop, push, rnd, Signo, slt, slti, sltiu, sltu, sub,
       sw, \xor , xori;
  wire [3:0] ALU_Select;
  wire [4:0] multiplexer_3_out, RD, RS, RT;
  wire [15:0] Constante;
  wire [25:0] Destino;
  wire [31:0] ALU_Output, con_extend_1_output, DATA_RF, g_instruction_1_output, HI, inPC, LO,
       multiplexer_1_out, outPC, random_1_out, RT_t, SP;
  wire [31:7] RS_t;

  or or_1 (or_1_out, lw, addi, sw);
  G_Instruction g_instruction_1 (
    .INPUT(in_2), .in_2(in_7), .Reset(Reset), .Enable(enableGI), .OUTPUT(g_instruction_1_output));
  Instruction_Decoder instruction_decoder_1 (
    .Instruccion(g_instruction_1_output), .nop(nop), .add(add), .andi(andi), .beq(beq), .sw(sw), .mfhi(mfhi),
    .pop(pop), .out_9(RS), .out_10(RT), .\and (\and ), .sub(sub), .ori(ori), .bne(bne), .jump(jump),
    .mflo(mflo), .push(push), .out_18(RD), .\or (\or ), .mult(mult), .xori(xori), .blez(blez), .jr(jr),
    .tty(tty), .\nor (\nor ), .mulu(mulu), .addi(addi), .bgtz(bgtz), .slt(slt), .rnd(rnd), .out_31(Destino),
    .\xor (\xor ), .div(div), .slti(slti), .bltz(bltz), .sltu(sltu), .kbd(kbd), .out_38(Constante),
    .divu(divu), .sltiu(sltiu), .lw(lw), .halt(halt));
  ALU_Selector alu_selector_1 (
    .in_1(add), .in_2(sub), .in_3(mult), .in_4(mulu), .in_5(div), .Signo(Signo), .in_6(divu), .in_7(slt),
    .in_8(sltu), .Inmediate(Inmediate), .in_9(\and ), .in_10(\or ), .in_11(\nor ), .in_12(\xor ),
    .in_13(or_1_out), .in_14(slti), .Selector(ALU_Select), .in_15(sltiu), .in_16(andi), .in_17(ori),
    .in_18(xori));
  Con_Extend con_extend_1 (.in_1(Constante), .ori(ori), .andi(andi), .xori(xori), .Output(con_extend_1_output));
  or or_2 (R_Inst, mfhi, rnd, tty, kbd, mflo);
  or or_3 (Stack_Inst, push, pop);
  or or_4 (Write_Inst, push, sw);
  or or_5 (Memory_Inst, lw, sw);
  Multiplexer #(.width(32), .enable("false")) multiplexer_1 (
    .in0(RT_t), .in1(con_extend_1_output), .out(multiplexer_1_out), .sel(Inmediate));
  ALU alu_1 (
    .Input1({RS_t, tty_Data}), .Input2(multiplexer_1_out), .in_3(Signo), .in_4(in_7), .in_5(ALU_Select),
    .Output(ALU_Output), .Lower(LO), .High(HI));
  or or_6 (ALU_Inst, add, \xor , addi, sltu, xori, sub, mult, slti, mulu, \or , ori, \and , \nor , div, divu, slt, sltiu, andi);
  PC pc_1 (.InPC(inPC), .OutPC(outPC), .Enable(enablePC), .Tic(in_7), .Reset(Reset));
  or or_7 (Jump_Inst, bgtz, blez, bne, beq, bltz, jump, jr, nop);
  Random #(.width(32)) random_1 (.clk(in_7), .next(rnd), .out(random_1_out));  // open: clr
  RF_Selector rf_selector_1 (
    .in_1(ALU_Output), .in_2(random_1_out), .LW(lw), .pop(pop), .mfhi(mfhi), .in_6(in_2), .OUTPUT(DATA_RF),
    .mflo(mflo), .actKBD(kbd), .in_9(HI), .actRND(rnd), .in_11(LO), .KBD(in_5));
  Memory_Addres memory_addres_1 (
    .in_1(ALU_Output), .pop(pop), .push(push), .in_4(outPC), .LW(lw), .SW(sw), .isPC(Next_instrc), .in_8(SP),
    .OUTPUT(ADDRESS));
  Multiplexer #(.width(32), .enable("false")) multiplexer_2 (
    .in0({RS_t, tty_Data}), .in1(RT_t), .out(R_Output), .sel(sw));
  Multiplexer #(.width(5)) multiplexer_3 (.in0(RD), .in1(RT), .out(multiplexer_3_out), .sel(Inmediate));  // open: en
  Register_File register_file_1 (
    .in_1(DATA_RF), .in_2(Reset), .in_3(in_7), .in_4(RF), .in_5(enablePC), .in_6(push), .in_7(pop),
    .in_8(multiplexer_3_out), .in_9(RS), .in_10(RT), .Output_B(RT_t), .Output_A({RS_t, tty_Data}), .SP(SP));
  Branch_Control branch_control_1 (
    .in_1(Destino), .beq(beq), .bne(bne), .in_4({RS_t, tty_Data}), .blez(blez), .bgtz(bgtz), .bltz(bltz),
    .in_8(RT_t), .jr(jr), .j(jump), .in_11(inPC), .in_12(Constante), .OUTPUT(outPC));

  // Other names for the same wires on the sheet: enGI = enableGI; enPC = enablePC; enRF = RF;
  //   Instruction[31:0] = in_2; Kbd_Data[6:0] = in_5; Next_In = Next_instrc; RS_t[6:0] = tty_Data; Tic = in_7

  // Notes on the sheet:
  //   INPUTS
  //   OUTPUTS
endmodule

module G_Instruction (
  input  [31:0] INPUT,
  input  in_2,
  input  Reset,
  input  Enable,
  output [31:0] OUTPUT
);

  wire [31:0] register_1_q;

  Register #(.width(32)) register_1 (.D(INPUT), .en(Enable), .Q(register_1_q), .clk(in_2), .clr(Reset));
  Inv inv_1 (.Input(register_1_q), .Output(OUTPUT));

  // Other names for the same wires on the sheet: Tic = in_2
endmodule

module Con_Extend (
  input  [15:0] in_1,
  input  ori,
  input  andi,
  input  xori,
  output [31:0] Output
);

  and and_1 (Output[31], in_1[15], ~ori, ~andi, ~xori);  // AND_Gate

  assign Output[30:0] = {{15{Output[31]}}, in_1};

  // Other names for the same wires on the sheet: Constante[15:0] = in_1
endmodule

module Control_Unit (
  input  Tic,
  input  tty_Inst,
  input  start,
  input  Ready_Data,
  input  Ready_Inst,
  input  ALU_Inst,
  input  jump_Inst,
  input  memor_Inst,
  input  R_Inst,
  input  Write_Inst,
  input  reset,
  input  Write_Ready,
  output out_13,
  output out_14,
  output out_15,
  output out_16,
  output en_tty,
  output out_18,
  output out_19,
  output out_20,
  output out_21
);

  wire branch, d_ff_1_q, d_ff_3_q, d_ff_4_q, d_ff_5_q, demultiplexer_1_out0, demultiplexer_1_out1, or_1_out,
       RF;
  wire [2:0] priority_encoder_1_out;

  Demultiplexer #(.select(3)) demultiplexer_1 (
    .out0(demultiplexer_1_out0), .out1(demultiplexer_1_out1), .out2(branch), .out3(RF), .out4(out_20),
    .out5(out_14), .in(d_ff_1_q), .sel(priority_encoder_1_out));  // open: out6, out7, en
  D_Flip_Flop #(.trigger("falling")) d_ff_1 (.clk(Tic), .D(Ready_Inst), .Q(d_ff_1_q));  // open: Qn, preset, en, reset
  Priority_Encoder priority_encoder_1 (
    .in0(1'b1), .in1(ALU_Inst), .in2(jump_Inst), .in3(R_Inst), .in4(memor_Inst), .in5(Write_Inst),
    .out(priority_encoder_1_out), .en_in(1'b1));  // open: in6, in7, gs, en_out
  D_Flip_Flop #(.trigger("falling")) d_ff_2 (
    .clk(Tic), .D(or_1_out), .Q(out_21), .reset(reset));  // open: Qn, preset, en
  or or_1 (or_1_out, out_21, demultiplexer_1_out0);
  and and_1 (en_tty, out_13, tty_Inst);
  D_Flip_Flop #(.trigger("falling")) d_ff_3 (
    .clk(Tic), .D(demultiplexer_1_out1), .Q(d_ff_3_q), .reset(reset));  // open: Qn, preset, en
  or or_2 (out_16, Ready_Data, d_ff_3_q, RF);
  D_Flip_Flop #(.trigger("falling")) d_ff_4 (
    .clk(Tic), .D(start), .Q(d_ff_4_q), .reset(reset));  // open: Qn, preset, en
  D_Flip_Flop #(.trigger("falling")) d_ff_5 (
    .clk(Tic), .D(out_15), .Q(d_ff_5_q), .reset(reset));  // open: Qn, preset, en
  or or_3 (out_18, d_ff_4_q, d_ff_5_q);
  D_Flip_Flop #(.trigger("falling")) d_ff_6 (.clk(Tic), .D(out_16), .Q(out_13));  // open: Qn, preset, en, reset
  or or_4 (out_15, out_13, Write_Ready, branch);

  assign out_19 = Ready_Inst;

  // Other names for the same wires on the sheet: count_PC = out_15; end = out_21; get_DATA = out_20;
  //   get_Inst = out_18; mem_Inst = memor_Inst; en_kbd = out_13; tty = out_13; use_GI = Ready_Inst; use_RF = out_16;
  //   write = out_14

  // Notes on the sheet:
  //   INPUTS
  //   OUTPUTS
endmodule

module Crono (
  input  in_1,
  input  in_2,
  input  in_3,
  input  [3:0] \time ,
  output Rready
);

  wire [3:0] counter_1_q;

  Counter #(.width(4), .max('hf)) counter_1 (
    .count(in_1), .Q(counter_1_q), .clk(in_3), .clr(in_2));  // open: load, D, carry
  Comparator #(.width(4)) comparator_1 (.a(\time ), .b(counter_1_q), .eq(Rready));  // open: gt, lt

  // Other names for the same wires on the sheet: reset = in_2; start = in_1; tic = in_3
endmodule

module Access_Ram (
  input  [31:0] RAM_0,
  input  in_2,
  input  Reset,
  input  Write,
  input  [31:0] RAM_1,
  input  GET,
  input  [3:0] R_Time,
  input  [31:0] RAM_2,
  input  [31:0] RAM_3,
  output [31:0] out_10,
  output ready,
  output [31:0] out_12,
  output Chip_Selecty,
  output [31:0] out_14,
  output [31:0] out_15
);

  wire crono_1_rready, or_1_out, S_I, Y;

  Register #(.width(32)) RAM0 (.D(RAM_0), .en(S_I), .Q(out_10), .clk(in_2), .clr(Reset));
  D_Flip_Flop #(.trigger("falling")) d_ff_1 (.clk(in_2), .D(GET), .Q(Y), .en(or_1_out));  // open: Qn, preset, reset
  or or_1 (or_1_out, GET, crono_1_rready);
  Register #(.width(32)) RAM1 (.D(RAM_1), .en(S_I), .Q(out_12), .clk(in_2), .clr(Reset));
  Crono crono_1 (.in_1(Y), .in_2(ready), .in_3(in_2), .\time (R_Time), .Rready(crono_1_rready));
  or or_2 (Chip_Selecty, S_I, Y);
  D_Flip_Flop #(.trigger("falling")) d_ff_2 (.clk(in_2), .D(crono_1_rready), .Q(S_I));  // open: Qn, preset, en, reset
  Register #(.width(32)) RAM2 (.D(RAM_2), .en(S_I), .Q(out_14), .clk(in_2), .clr(Reset));
  D_Flip_Flop #(.trigger("falling")) d_ff_3 (.clk(in_2), .D(S_I), .Q(ready));  // open: Qn, preset, en, reset
  Register #(.width(32)) RAM3 (.D(RAM_3), .en(S_I), .Q(out_15), .clk(in_2), .clr(Reset));

  // Other names for the same wires on the sheet: RAM_Out0[31:0] = out_10; RAM_Out1[31:0] = out_12;
  //   RAM_Out2[31:0] = out_14; RAM_Out3[31:0] = out_15; Tic = in_2

  // Notes on the sheet:
  //   INPUTS
  //   INPUTS
  //   OUTPUTS
endmodule

module Using_RAM (
  input  [31:0] RAM_0,
  input  Tic,
  input  Reset,
  input  Write,
  input  [31:0] RAM_1,
  input  get_Ins,
  input  get_DATA,
  input  is_Ins,
  input  [31:0] RAM_2,
  input  [31:0] RAM_3,
  input  [31:0] DP_Address,
  input  [3:0] Write_Time,
  input  [3:0] Read_Time,
  output [31:0] out_14,
  output R_W,
  output [31:0] out_16,
  output Chip_Selecty,
  output [31:0] out_18,
  output Rd_Inst,
  output Rd_Data,
  output Rd_Write,
  output [31:0] out_22,
  output [15:0] ADDR,
  output [3:0] MASK
);

  wire crono_1_rready, CS_Dat, CS_Ins, or_1_out;
  wire [31:0] Dat_O0, Dat_O1, Dat_O2, Dat_O3, Ins_O0, Ins_O1, Ins_O2, Ins_O3, inv_1_output, inv_2_output,
       inv_3_output, inv_4_output;

  D_Flip_Flop #(.trigger("falling")) d_ff_1 (.clk(Tic), .D(Write), .Q(R_W), .en(or_1_out));  // open: Qn, preset, reset
  or or_1 (or_1_out, Write, crono_1_rready);
  Crono crono_1 (.in_1(R_W), .in_2(Rd_Write), .in_3(Tic), .\time (Write_Time), .Rready(crono_1_rready));
  or or_2 (Chip_Selecty, CS_Ins, R_W, Rd_Write);
  D_Flip_Flop #(.trigger("falling")) d_ff_2 (
    .clk(Tic), .D(crono_1_rready), .Q(Rd_Write));  // open: Qn, preset, en, reset
  Demultiplexer #(.select(2)) demultiplexer_1 (
    .out0(MASK[0]), .out1(MASK[1]), .out2(MASK[2]), .out3(MASK[3]), .in(1'b1), .sel(DP_Address[3:2]));  // open: en
  Access_Ram access_ram_1 (
    .RAM_0(RAM_0), .in_2(Tic), .Reset(Reset), .Write(Write), .RAM_1(RAM_1), .GET(get_DATA),
    .R_Time(Read_Time), .RAM_2(RAM_2), .RAM_3(RAM_3), .out_10(Dat_O0), .ready(Rd_Data), .out_12(Dat_O1),
    .Chip_Selecty(CS_Dat), .out_14(Dat_O2), .out_15(Dat_O3));
  Inv inv_1 (.Input(Dat_O0), .Output(inv_1_output));
  Inv inv_2 (.Input(Dat_O1), .Output(inv_2_output));
  Inv inv_3 (.Input(Dat_O2), .Output(inv_3_output));
  Inv inv_4 (.Input(Dat_O3), .Output(inv_4_output));
  Multiplexer #(.width(32)) multiplexer_1 (.in0(inv_1_output), .in1(Ins_O0), .out(out_14), .sel(is_Ins));  // open: en
  Multiplexer #(.width(32)) multiplexer_2 (.in0(inv_2_output), .in1(Ins_O1), .out(out_16), .sel(is_Ins));  // open: en
  Multiplexer #(.width(32)) multiplexer_3 (.in0(inv_3_output), .in1(Ins_O2), .out(out_18), .sel(is_Ins));  // open: en
  Multiplexer #(.width(32)) multiplexer_4 (.in0(inv_4_output), .in1(Ins_O3), .out(out_22), .sel(is_Ins));  // open: en
  Access_Ram access_ram_2 (
    .RAM_0(RAM_0), .in_2(Tic), .Reset(Reset), .Write(Write), .RAM_1(RAM_1), .GET(get_Ins),
    .R_Time(Read_Time), .RAM_2(RAM_2), .RAM_3(RAM_3), .out_10(Ins_O0), .ready(Rd_Inst), .out_12(Ins_O1),
    .Chip_Selecty(CS_Ins), .out_14(Ins_O2), .out_15(Ins_O3));

  assign ADDR = DP_Address[19:4];

  // Other names for the same wires on the sheet: RAM_Out0[31:0] = out_14; RAM_Out1[31:0] = out_16;
  //   RAM_Out2[31:0] = out_18; RAM_Out3[31:0] = out_22

  // Notes on the sheet:
  //   INPUTS
  //   INPUTS
  //   OUTPUTS
  //   DATA
  //   write aun no cumple funcion dentro de access ram, futuro testeo
  //   INSTRUCTION
endmodule
